# Fritzing sketch EMU (saved by Fritzing 0.9.3b)
breadboards: 1

parts:
  Part1 = Adafruit Feather 32u4 RFM9xW LoRa [part_number="Adafruit #3078 and Adafruit #3079"]
  Part2 = Adafruit_BMP280
  U1 = LIPO-2000mAh [package=lipo-2000]
  J1 = Power Jack [package=power_jack_smd]
  Part3 = Adafruit USB DC Solar LiPo Charger [part_number="Adafruit #390"]

nets:
  N1: Part1.DIO1, Part1.6
  GND: Part1.GND, Part2.GND, U1.-, J1.GNDBREAK, Part3.GND
  +3V3: Part1.+3V3, Part2.3.3V
  N2: Part1.VBAT, Part3.LOAD
  N3: Part1.3, Part2.SCK/SCL
  N4: Part1.2, Part2.SDI/SDA
  N5: U1.+, Part3.BATT
  N6: J1.PWR, Part3.DCIN

custom parts:
  Adafruit Feather 32u4 RFM9xW LoRa: This is the Adafruit Feather 32u4 LoRa Radio (RFM9x) - our take on an microcontroller with a "Long Range (LoRa)" packet radio transceiver with built in USB and battery charging. Its an Adafruit Feather 32u4 with a 868/915 MHz radio module cooked in! Great for making wireless networks that can go further than 2.4GHz 802.15.4 and similar, are more flexible than Bluetooth LE and without the high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
  Adafruit_BMP280: Bosch has stepped up their game with their new BMP280 sensor, an environmental sensor with temperature, barometric pressure that is the next generation upgrade to the BMP085/BMP180/BMP183. This sensor is great for all sorts of weather sensing and can even be used in both I2C and SPI! This precision sensor from Bosch is the best low-cost, precision sensing solution for measuring barometric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
  Adafruit USB DC Solar LiPo Charger: Make your projects to go green this summer with our specialized USB/Solar Lithium Ion Polymer Battery charger! This charger is a very unique design, perfect for outdoor projects, or DIY iPod chargers. We've spent over a year testing and tinkering with this charger to come up with a plug and play solution to charging batteries with the sun and we're really pleased with what we ended up with.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
