# Fritzing sketch SignalTracker (saved by Fritzing 0.9.3b)
breadboards: 1

parts:
  Part1 = Adafruit Feather 32u4 RFM9xW LoRa [part_number="Adafruit #3078 and Adafruit #3079"]
  S1 = Pushbutton [package="[THT]"]
  S2 = Taiway 100-SP-X-T1 SPDT Miniature Toggle Switch [part_number=100-SP-X-T1-0-0-B1-M1 package=THT]
  U1 = LIPO-2000mAh [package=lipo-2000]
  R1 = Resistor [tolerance=±5% resistance=220 package=THT]
  LED1 = LED - 5mm [color="Red (633nm)" package="5 mm [THT]"]

nets:
  N1: Part1.DIO1, Part1.6
  N2: Part1.GND, S1.Pin_1, S1.Pin_2, U1.-, R1.Pin_1
  N3: Part1.VBAT, S2.COM
  N4: Part1.13, LED1.anode
  N5: Part1.10, S1.Pin_3, S1.Pin_4
  N6: S2.L2, U1.+
  N7: R1.Pin_0, LED1.cathode

notes:
  Antenna 82.1 mm

custom parts:
  Adafruit Feather 32u4 RFM9xW LoRa: This is the Adafruit Feather 32u4 LoRa Radio (RFM9x) - our take on an microcontroller with a "Long Range (LoRa)" packet radio transceiver with built in USB and battery charging. Its an Adafruit Feather 32u4 with a 868/915 MHz radio module cooked in! Great for making wireless networks that can go further than 2.4GHz 802.15.4 and similar, are more flexible than Bluetooth LE and without the high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
